# Fritzing sketch Scheme (saved by Fritzing 0.9.3b)
breadboards: 1

parts:
  CPU1 = NodeMCU WROOM ESP 32
  LED1 = LED - 5mm [color="Red (633nm)" package="5 mm [THT]"]
  S1 = Tactile switch 12mm [package=THT]
  S2 = Tactile switch 12mm [package=THT]
  R1 = Resistor [tolerance=±5% resistance=2.2k package=THT]
  R2 = Resistor [tolerance=±5% resistance=2.2k package=THT]
  LED2 = LED - 5mm [color="Red (633nm)" package="5 mm [THT]"]
  LED3 = LED - 5mm [color="Red (633nm)" package="5 mm [THT]"]
  R3 = Resistor [tolerance=±5% resistance=220 package="0603 [SMD]"]
  R4 = Resistor [tolerance=±5% resistance=220 package="0603 [SMD]"]
  R5 = Resistor [tolerance=±5% resistance=220 package="0603 [SMD]"]

nets:
  N1: CPU1.pin_8, CPU1.pin_24, CPU1.pin_28, LED1.anode
  N2: CPU1.pin_9, CPU1.pin_25
  N3: CPU1.pin_17, S1.1, S1.2, S2.1, S2.2
  N4: CPU1.pin_18, R1.Pin_1, R2.Pin_1, R3.Pin_1, R4.Pin_0, R5.Pin_0
  N5: CPU1.pin_21, LED2.anode
  N6: CPU1.pin_26, LED3.anode
  N7: CPU1.pin_30, S1.3, S1.4, R2.Pin_0
  N8: LED1.cathode, R5.Pin_1
  N9: S2.3, S2.4, R1.Pin_0
  N10: LED2.cathode, R4.Pin_1
  N11: LED3.cathode, R3.Pin_0

custom parts:
  NodeMCU WROOM ESP 32: 30 pol Development Kit
  Tactile switch 12mm: 12 mm tactile switch (push button/momentary switch) from the B3F family.
  Tactile switch 12mm: 12 mm tactile switch (push button/momentary switch) from the B3F family.
